// Logisim project e2633501 (1).circ as structural Verilog: 1 circuit, main circuit main
module main (
  input  A0,
  input  A1,
  input  B0,
  input  B1,
  output X,
  output Y,
  output Z
);

  wire and_1_out, and_2_out, and_3_out, and_4_out, and_5_out, and_6_out, and_7_out, and_8_out, and_9_out,
       and_10_out, and_11_out, and_12_out, and_13_out, not_1_out, not_2_out, not_3_out, not_4_out, or_1_out,
       or_2_out;

  not not_1 (not_1_out, A0);
  not not_2 (not_2_out, A1);
  not not_3 (not_3_out, B0);
  not not_4 (not_4_out, B1);
  and and_1 (and_1_out, not_4_out, B0);
  and and_2 (and_2_out, A0, not_2_out);
  and and_3 (and_3_out, B1, B0);
  and and_4 (and_4_out, not_4_out, not_2_out);
  and and_5 (and_5_out, A1, not_1_out);
  and and_6 (and_6_out, B1, not_3_out);
  and and_7 (and_7_out, and_5_out, B0);
  and and_8 (and_8_out, and_1_out, and_2_out);
  and and_9 (and_9_out, and_5_out, and_6_out);
  and and_10 (and_10_out, and_6_out, A0);
  or or_1 (or_1_out, and_10_out, and_7_out);
  and and_11 (and_11_out, A0, A1);
  and and_12 (and_12_out, A1, not_4_out);
  or or_2 (or_2_out, and_4_out, and_9_out);
  or or_3 (Z, or_1_out, and_8_out);
  and and_13 (and_13_out, and_11_out, and_3_out);
  or or_4 (X, and_11_out, and_12_out);
  or or_5 (Y, and_13_out, or_2_out);
endmodule
