// Logisim project e2633501.circ as structural Verilog: 1 circuit, main circuit main
module main (
  input  S2,
  input  S1,
  input  S0,
  input  A0,
  input  A1,
  input  A2,
  input  A3,
  output L0,
  output L1,
  output L2,
  output L3,
  output L4,
  output L5,
  output L6,
  output L7
);

  wire and_1_out, and_2_out, and_3_out, and_4_out, and_5_out, and_6_out, and_7_out, and_8_out, and_9_out,
       and_10_out, and_11_out, and_12_out, and_13_out, and_14_out, and_15_out, and_16_out,
       n3_to_8_decoder_74138_2_p4, n3_to_8_decoder_74138_3_p4, n4_to_1_mux_x2_74153_1_p10,
       n4_to_1_mux_x2_74153_1_p11, n4_to_1_mux_x2_74153_2_p10, n4_to_1_mux_x2_74153_2_p11,
       n4_to_1_mux_x2_74153_3_p10, n4_to_1_mux_x2_74153_3_p11, n4_to_1_mux_x2_74153_4_p10,
       n4_to_1_mux_x2_74153_4_p11, n4_to_1_mux_x2_74153_5_p10, n4_to_1_mux_x2_74153_5_p11,
       n4_to_1_mux_x2_74153_6_p10, n4_to_1_mux_x2_74153_6_p11, n4_to_1_mux_x2_74153_7_p10,
       n4_to_1_mux_x2_74153_7_p11, n4_to_1_mux_x2_74153_8_p10, n4_to_1_mux_x2_74153_8_p11, not_3_out,
       not_4_out, not_5_out, not_6_out, not_7_out, not_8_out, not_9_out, not_10_out, not_11_out, not_12_out,
       not_13_out, not_14_out, not_15_out, not_16_out, not_17_out, not_18_out, not_19_out, not_20_out,
       not_21_out, not_22_out, not_23_out, not_24_out, not_25_out, not_26_out, not_27_out, not_28_out,
       not_29_out, not_30_out, not_31_out, not_32_out, not_33_out, not_34_out, not_35_out, not_36_out,
       not_37_out, not_38_out, not_39_out, not_40_out, not_41_out, not_42_out, not_43_out, not_44_out,
       not_45_out, not_46_out, not_47_out, not_48_out, not_49_out, not_50_out, or_1_out, or_2_out, or_3_out,
       or_4_out, or_5_out, or_6_out, or_7_out, or_8_out, or_9_out, or_10_out, or_11_out, or_12_out,
       or_13_out, or_14_out, or_15_out, or_16_out, or_17_out, or_18_out, or_19_out, or_20_out, or_21_out,
       or_22_out, or_23_out, or_24_out, or_25_out, or_26_out, or_27_out, or_28_out, or_29_out, or_30_out,
       or_31_out, or_32_out;

  // _3_to_8_decoder__74138 #(.Facing("east")) 3_to_8_decoder_74138_1: pin names not known; wires that end beside it: A0, A1, A2, A3, 1'b0, 1'b0
  // _3_to_8_decoder__74138 #(.Facing("east")) 3_to_8_decoder_74138_2: pin names not known; wires that end beside it: A0, A1, A2, n3_to_8_decoder_74138_2_p4, 1'b0, 1'b0
  not not_1 (n3_to_8_decoder_74138_2_p4, A3);
  // _3_to_8_decoder__74138 #(.Facing("east")) 3_to_8_decoder_74138_3: pin names not known; wires that end beside it: A0, A1, A2, n3_to_8_decoder_74138_3_p4, 1'b0, 1'b0
  not not_2 (n3_to_8_decoder_74138_3_p4, A3);
  // NOT_Gate not_3 has open pins: in=open, out=not_3_out
  // NOT_Gate not_4 has open pins: in=open, out=not_4_out
  // NOT_Gate not_5 has open pins: in=open, out=not_5_out
  // NOT_Gate not_6 has open pins: in=open, out=not_6_out
  // NOT_Gate not_7 has open pins: in=open, out=not_7_out
  // NOT_Gate not_8 has open pins: in=open, out=not_8_out
  // NOT_Gate not_9 has open pins: in=open, out=not_9_out
  // NOT_Gate not_10 has open pins: in=open, out=not_10_out
  // NOT_Gate not_11 has open pins: in=open, out=not_11_out
  // NOT_Gate not_12 has open pins: in=open, out=not_12_out
  // NOT_Gate not_13 has open pins: in=open, out=not_13_out
  // NOT_Gate not_14 has open pins: in=open, out=not_14_out
  // NOT_Gate not_15 has open pins: in=open, out=not_15_out
  // NOT_Gate not_16 has open pins: in=open, out=not_16_out
  // NOT_Gate not_17 has open pins: in=open, out=not_17_out
  // NOT_Gate not_18 has open pins: in=open, out=not_18_out
  // NOT_Gate not_19 has open pins: in=open, out=not_19_out
  // NOT_Gate not_20 has open pins: in=open, out=not_20_out
  // NOT_Gate not_21 has open pins: in=open, out=not_21_out
  // NOT_Gate not_22 has open pins: in=open, out=not_22_out
  // NOT_Gate not_23 has open pins: in=open, out=not_23_out
  // NOT_Gate not_24 has open pins: in=open, out=not_24_out
  // NOT_Gate not_25 has open pins: in=open, out=not_25_out
  // NOT_Gate not_26 has open pins: in=open, out=not_26_out
  // _3_to_8_decoder__74138 #(.Facing("east")) 3_to_8_decoder_74138_4: pin names not known; wires that end beside it: A1, A2, A0, A1, A2, A3, 1'b0, 1'b0
  // _3_to_8_decoder__74138 #(.Facing("east")) 3_to_8_decoder_74138_5: pin names not known; wires that end beside it: A0, A1, A2, 1'b1, 1'b0, 1'b0
  // NOT_Gate not_27 has open pins: in=open, out=not_27_out
  // NOT_Gate not_28 has open pins: in=open, out=not_28_out
  // NOT_Gate not_29 has open pins: in=open, out=not_29_out
  // NOT_Gate not_30 has open pins: in=open, out=not_30_out
  // NOT_Gate not_31 has open pins: in=open, out=not_31_out
  // NOT_Gate not_32 has open pins: in=open, out=not_32_out
  // NOT_Gate not_33 has open pins: in=open, out=not_33_out
  // NOT_Gate not_34 has open pins: in=open, out=not_34_out
  // NOT_Gate not_35 has open pins: in=open, out=not_35_out
  // NOT_Gate not_36 has open pins: in=open, out=not_36_out
  // NOT_Gate not_37 has open pins: in=open, out=not_37_out
  // NOT_Gate not_38 has open pins: in=open, out=not_38_out
  // NOT_Gate not_39 has open pins: in=open, out=not_39_out
  // NOT_Gate not_40 has open pins: in=open, out=not_40_out
  // NOT_Gate not_41 has open pins: in=open, out=not_41_out
  // NOT_Gate not_42 has open pins: in=open, out=not_42_out
  or or_1 (or_1_out, not_3_out, not_5_out);
  or or_2 (or_2_out, not_7_out, not_9_out);
  or or_3 (or_3_out, not_11_out, not_10_out);
  or or_4 (or_4_out, not_12_out, not_13_out);
  or or_5 (or_5_out, not_4_out, not_6_out);
  or or_6 (or_6_out, not_15_out, not_18_out);
  or or_7 (or_7_out, not_14_out, not_8_out);
  or or_8 (or_8_out, not_16_out, not_17_out);
  or or_9 (or_9_out, not_5_out, not_9_out);
  or or_10 (or_10_out, not_20_out, not_22_out);
  or or_11 (or_11_out, not_21_out, not_3_out);
  or or_12 (or_12_out, not_26_out, not_8_out);
  or or_13 (or_13_out, not_25_out, not_6_out);
  or or_14 (or_14_out, not_19_out, not_24_out);
  or or_15 (or_15_out, not_4_out, not_7_out);
  or or_16 (or_16_out, not_23_out, not_10_out);
  or or_17 (or_17_out, not_31_out, not_33_out);
  or or_18 (or_18_out, not_20_out, not_27_out);
  or or_19 (or_19_out, not_24_out, not_25_out);
  or or_20 (or_20_out, not_21_out, not_30_out);
  or or_21 (or_21_out, not_19_out, not_34_out);
  or or_22 (or_22_out, not_22_out, not_32_out);
  or or_23 (or_23_out, not_28_out, not_29_out);
  or or_24 (or_24_out, not_23_out, not_26_out);
  or or_25 (or_25_out, not_7_out, not_9_out);
  or or_26 (or_26_out, not_12_out, not_3_out);
  or or_27 (or_27_out, not_16_out, not_17_out);
  or or_28 (or_28_out, not_13_out, not_6_out);
  or or_29 (or_29_out, not_11_out, not_10_out);
  or or_30 (or_30_out, not_14_out, not_8_out);
  or or_31 (or_31_out, not_4_out, not_5_out);
  or or_32 (or_32_out, not_15_out, not_18_out);
  // _4_to_1_MUX__x2___74153 #(.Facing("east")) 4_to_1_mux_x2_74153_1: pin names not known; wires that end beside it: or_25_out, or_1_out, not_42_out, or_9_out, or_17_out, 1'b0, S0, 1'b0, S1, n4_to_1_mux_x2_74153_1_p10, n4_to_1_mux_x2_74153_1_p11
  // _4_to_1_MUX__x2___74153 #(.Facing("east")) 4_to_1_mux_x2_74153_2: pin names not known; wires that end beside it: or_26_out, or_2_out, not_41_out, or_10_out, or_18_out, 1'b0, S0, 1'b0, S1, n4_to_1_mux_x2_74153_2_p10, n4_to_1_mux_x2_74153_2_p11
  // _4_to_1_MUX__x2___74153 #(.Facing("east")) 4_to_1_mux_x2_74153_3: pin names not known; wires that end beside it: or_27_out, or_3_out, not_40_out, or_11_out, or_19_out, 1'b0, S0, 1'b0, S1, n4_to_1_mux_x2_74153_3_p10, n4_to_1_mux_x2_74153_3_p11
  // _4_to_1_MUX__x2___74153 #(.Facing("east")) 4_to_1_mux_x2_74153_4: pin names not known; wires that end beside it: or_28_out, or_4_out, not_39_out, or_12_out, or_20_out, 1'b0, S0, 1'b0, S1, n4_to_1_mux_x2_74153_4_p10, n4_to_1_mux_x2_74153_4_p11
  // _4_to_1_MUX__x2___74153 #(.Facing("east")) 4_to_1_mux_x2_74153_5: pin names not known; wires that end beside it: or_29_out, or_5_out, not_38_out, or_13_out, or_21_out, 1'b0, S0, 1'b0, S1, n4_to_1_mux_x2_74153_5_p10, n4_to_1_mux_x2_74153_5_p11
  // _4_to_1_MUX__x2___74153 #(.Facing("east")) 4_to_1_mux_x2_74153_6: pin names not known; wires that end beside it: or_30_out, or_6_out, not_37_out, or_14_out, or_22_out, 1'b0, S0, 1'b0, S1, n4_to_1_mux_x2_74153_6_p10, n4_to_1_mux_x2_74153_6_p11
  // _4_to_1_MUX__x2___74153 #(.Facing("east")) 4_to_1_mux_x2_74153_7: pin names not known; wires that end beside it: or_31_out, or_7_out, not_36_out, or_15_out, or_23_out, 1'b0, S0, 1'b0, S1, n4_to_1_mux_x2_74153_7_p10, n4_to_1_mux_x2_74153_7_p11
  // _4_to_1_MUX__x2___74153 #(.Facing("east")) 4_to_1_mux_x2_74153_8: pin names not known; wires that end beside it: or_32_out, or_8_out, not_35_out, or_16_out, or_24_out, 1'b0, S0, 1'b0, S1, n4_to_1_mux_x2_74153_8_p10, n4_to_1_mux_x2_74153_8_p11
  not not_43 (not_43_out, S2);
  and and_1 (and_1_out, not_43_out, n4_to_1_mux_x2_74153_1_p10);
  and and_2 (and_2_out, S2, n4_to_1_mux_x2_74153_1_p11);
  not not_44 (not_44_out, S2);
  and and_3 (and_3_out, not_44_out, n4_to_1_mux_x2_74153_2_p10);
  and and_4 (and_4_out, S2, n4_to_1_mux_x2_74153_2_p11);
  not not_45 (not_45_out, S2);
  and and_5 (and_5_out, not_45_out, n4_to_1_mux_x2_74153_3_p10);
  and and_6 (and_6_out, S2, n4_to_1_mux_x2_74153_3_p11);
  not not_46 (not_46_out, S2);
  and and_7 (and_7_out, not_46_out, n4_to_1_mux_x2_74153_4_p10);
  and and_8 (and_8_out, S2, n4_to_1_mux_x2_74153_4_p11);
  not not_47 (not_47_out, S2);
  and and_9 (and_9_out, not_47_out, n4_to_1_mux_x2_74153_5_p10);
  and and_10 (and_10_out, S2, n4_to_1_mux_x2_74153_5_p11);
  not not_48 (not_48_out, S2);
  and and_11 (and_11_out, not_48_out, n4_to_1_mux_x2_74153_6_p10);
  and and_12 (and_12_out, S2, n4_to_1_mux_x2_74153_6_p11);
  not not_49 (not_49_out, S2);
  and and_13 (and_13_out, not_49_out, n4_to_1_mux_x2_74153_7_p10);
  and and_14 (and_14_out, S2, n4_to_1_mux_x2_74153_7_p11);
  not not_50 (not_50_out, S2);
  and and_15 (and_15_out, not_50_out, n4_to_1_mux_x2_74153_8_p10);
  and and_16 (and_16_out, S2, n4_to_1_mux_x2_74153_8_p11);
  or or_33 (L0, and_1_out, and_2_out);
  or or_34 (L1, and_3_out, and_4_out);
  or or_35 (L2, and_5_out, and_6_out);
  or or_36 (L3, and_7_out, and_8_out);
  or or_37 (L4, and_9_out, and_10_out);
  or or_38 (L5, and_11_out, and_12_out);
  or or_39 (L6, and_13_out, and_14_out);
  or or_40 (L7, and_15_out, and_16_out);
endmodule
